# Fritzing sketch Fritzing Pinout (saved by Fritzing 0.9.10b)

parts:
  Part1 = BH1750
  Part2 = Arduino Uno (Rev3) - ICSP
  LCD2004-I2C1 = LCD2004-I2C
  HC-SR04_Sensor_1 = HC-SR04 Ultrasonic Distance Sensor
  Bauteil1 = Humidity Sensor - HIH-4030 Breakout
  Mod1 = KY-019 5V Relay Module [package="Breakout board"]
  Mod2 = KY-019 5V Relay Module [package="Breakout board"]
  Mod3 = KY-019 5V Relay Module [package="Breakout board"]
  DS1 = DS18B20 1-Wire Temperature Sensor [part_number=DS18B20]
  DS2 = DS18B20 1-Wire Temperature Sensor [part_number=DS18B20]
  R1 = 4,7 kΩ Resistor [package=THT]
  R2 = 4,7 kΩ Resistor [package=THT]

nets:
  VCC: Part1.VCC, Part2.5V, LCD2004-I2C1.VCC, HC-SR04_Sensor_1.VCC, Bauteil1.VCC
  GND: Part1.GND, Part2.GND, HC-SR04_Sensor_1.GND, Bauteil1.GND
  N1: Part1.SCL, Part2.A5/SCL, LCD2004-I2C1.SCL
  N2: Part1.SDA, Part2.A4/SDA, LCD2004-I2C1.SDA
  N3: Part2.D8, Mod3.S
  N4: Part2.D9_PWM, Mod2.S
  N5: Part2.D10_PWM/SS, Mod1.S
  N6: Part2.D11_PWM/MOSI, HC-SR04_Sensor_1.TRIG
  N7: Part2.D12/MISO, HC-SR04_Sensor_1.ECHO
  N8: Part2.D2, DS2.DQ, R2.Pin_0
  N9: Part2.D4, DS1.DQ, R1.Pin_0
  N10: Part2.D7, Bauteil1.OUT
  N11: DS2.VDD, R2.Pin_1

custom parts:
  BH1750: Light Sensor
  LCD2004-I2C: A standard character display with 4x20 characters. Comes in many colors with LCM2004 IIC attached.
  KY-019 5V Relay Module: KY-019 5V Relay module, used to control AC circuits. (Special thanks to vanepp for fixing the PCB holes and other errors)
  4,7 kΩ Resistor: A generic resistor (0.25W)
